// Logisim project elements.circ as structural Verilog: 5 circuits, main circuit NAND
module NAND (
  input  a,
  input  b,
  output out
);

  nand nand_1 (out, a, b);
endmodule

module NOT (
  input  in,
  output out
);

  nand nand_1 (out, in, in);
endmodule

module AND (
  input  a,
  input  b,
  output out
);

  wire nand_1_out;

  nand nand_1 (nand_1_out, a, b);
  nand nand_2 (out, nand_1_out, nand_1_out);
endmodule

module OR (
  input  a,
  input  b,
  output out
);

  wire nand_1_out, nand_2_out;

  nand nand_1 (nand_1_out, a, a);
  nand nand_2 (nand_2_out, b, b);
  nand nand_3 (out, nand_1_out, nand_2_out);
endmodule

module XOR (
  input  a,
  input  b,
  output out
);

  wire nand_1_out;

  nand nand_1 (nand_1_out, a, b);
  // NAND_Gate nand_2 is placed but not wired
  // NAND_Gate nand_3 has open pins: in0=nand_1_out, in1=nand_1_out, out=open
endmodule
